# Fritzing sketch bootboots (saved by Fritzing 1.0.6)
circuit board: 6.5564cm x 8.75488cm
breadboards: 2

parts:
  470µF = Capacitor Polarized [package=cpol-radial-1000uf-25v]
  PCF8574 = PCF8574 [package="DIP16 [THT]"]
  Hex_Inv1 = 74HC04_HEX_INVERTER [package=dil14]
  Spray = RELAY-SOLIDSTATE [package=relay-s108t02]
  Spray_2 = Camdenboss CTB0158-2 [part_number=CTB0158-2 package=THT]
  LED1 = Camdenboss CTB0158-2 [part_number=CTB0158-2 package=THT]
  LED = RELAY-SOLIDSTATE [package=relay-s108t02]
  5V = Camdenboss CTB0158-2 [part_number=CTB0158-2 package=THT]
  ESP32-S3_Cam = ESP32-S3-Wroom-board-Freenove_1
  Light_Sensor = Infrared Proximity Sensor [distance_to_obstacle=50%]
  GPIO41 = Camdenboss CTB0158-2 [part_number=CTB0158-2 package=THT]
  GPIO42 = Camdenboss CTB0158-2 [part_number=CTB0158-2 package=THT]
  10kΩ = Resistor [tolerance=±5% power=0.25W resistance=220 package=THT]

nets:
  GND: 470µF.+, PCF8574.A0, PCF8574.A1, PCF8574.A2, PCF8574.P0, PCF8574.P1, PCF8574.P2, PCF8574.GND, PCF8574.P4, PCF8574.P6, PCF8574.P7, PCF8574.INT, Hex_Inv1.3A, Hex_Inv1.3Y, Hex_Inv1.GND, Hex_Inv1.4Y, Hex_Inv1.4A, Spray.-, LED.+, ESP32-S3_Cam.connector20, Light_Sensor.GND, GPIO41.pin2, GPIO42.pin2
  N1: 470µF.-, Spray.+, 10kΩ.Pin_1
  N2: PCF8574.P3, Hex_Inv1.1A, Hex_Inv1.2A
  N3: PCF8574.P5, Hex_Inv1.5A, Hex_Inv1.6A
  N4: PCF8574.SCL, ESP32-S3_Cam.connector23
  N5: PCF8574.SDA, ESP32-S3_Cam.connector24
  VCC: PCF8574.VCC, Hex_Inv1.VCC, ESP32-S3_Cam.connector0, Light_Sensor.Vout
  N6: Hex_Inv1.1Y, Hex_Inv1.2Y, 10kΩ.Pin_0
  N7: Hex_Inv1.5Y, Hex_Inv1.6Y, LED.-
  N8: Spray.T1, Spray_2.pin1
  N9: Spray.T2, LED.T2, 5V.pin1
  N10: Spray_2.pin2, LED1.pin2, 5V.pin2
  N11: LED1.pin1, LED.T1
  N12: ESP32-S3_Cam.connector34, GPIO41.pin1
  N13: ESP32-S3_Cam.connector35, GPIO42.pin1
  N14: ESP32-S3_Cam.connector37, Light_Sensor.Vcc

notes:
  Designed by Nakomis
  Boot the Boots!
