# Fritzing sketch bootboots (saved by Fritzing 1.0.6)
circuit board: 6.5564cm x 8.75488cm
breadboards: 1

parts:
  470µF = Capacitor Polarized [package=cpol-radial-1000uf-25v]
  Hex_Inv1 = 74HC04_HEX_INVERTER [package=dil14]
  Spray = Camdenboss CTB0158-2 [part_number=CTB0158-2 package=THT]
  LEDs = Camdenboss CTB0158-2 [part_number=CTB0158-2 package=THT]
  5V = Camdenboss CTB0158-2 [part_number=CTB0158-2 package=THT]
  ESP32-S3_Cam = ESP32-S3-Wroom-board-Freenove_1
  GPIO41 = Camdenboss CTB0158-2 [part_number=CTB0158-2 package=THT]
  PIR = Camdenboss CTB0158-2 [part_number=CTB0158-2 package=THT]
  PCF8574 = PCF8574 [package="DIP16 [THT]"]
  10kΩ = Resistor [tolerance=±5% power=0.25W resistance=220 package=THT]
  Spray_2 = NakSSDDC
  LEDs_2 = NakSSDDC

nets:
  N1: 470µF.+, 10kΩ.Pin_1, Spray_2.connector2
  GND: 470µF.-, Hex_Inv1.GND, Spray.pin2, LEDs.pin2, 5V.pin2, ESP32-S3_Cam.connector20, PCF8574.A0, PCF8574.A1, PCF8574.A2, PCF8574.P0, PCF8574.P1, PCF8574.P2, PCF8574.GND, PCF8574.P4, PCF8574.P6, PCF8574.P7, PCF8574.INT, Spray_2.connector3, LEDs_2.connector3
  N2: Hex_Inv1.1A, Hex_Inv1.2A, PCF8574.P3
  N3: Hex_Inv1.1Y, Hex_Inv1.2Y, 10kΩ.Pin_0
  N4: Hex_Inv1.5Y, Hex_Inv1.6Y, LEDs_2.connector2
  N5: Hex_Inv1.5A, Hex_Inv1.6A, PCF8574.P5
  VCC: Hex_Inv1.VCC, ESP32-S3_Cam.connector0, GPIO41.pin1, PCF8574.VCC
  N6: Spray.pin1, Spray_2.connector0
  N7: LEDs.pin1, LEDs_2.connector0
  N8: 5V.pin1, PIR.pin1, Spray_2.connector1, LEDs_2.connector1
  N9: ESP32-S3_Cam.connector23, PCF8574.SCL
  N10: ESP32-S3_Cam.connector24, PCF8574.SDA
  N11: ESP32-S3_Cam.connector34, GPIO41.pin2
  N12: ESP32-S3_Cam.connector35, PIR.pin2

notes:
  Designed by Nakomis
  Boot the Boots!
